# Fritzing sketch 1 (saved by Fritzing 0.9.3b)
breadboards: 1

parts:
  LM741 = LM386 [package=dip08]
  R1 = Resistor [tolerance=±5% resistance=47k package=THT]
  R2 = Resistor [tolerance=±5% resistance=100k package=THT]
  R3 = Rotary Potentiometer (Small) [maximum_resistance=100k package=THT]
  T2 = Resistor [tolerance=±5% resistance=100k package=THT]
  T1 = Resistor [tolerance=±5% resistance=100k package=THT]
  J1 = female pin header, 2 pins [form="♀ (female)"]

nets:
  N1: LM741.-IN, R1.Pin_1, T1.Pin_0
  N2: LM741.+IN, R2.Pin_1, T2.Pin_0
  GND: LM741.V-, R2.Pin_0, R3.wiper, J1.pin2
  N3: LM741.OUT, J1.pin1
  12V: LM741.V+, T2.Pin_1, T1.Pin_1
  N4: R1.Pin_0, R3.leg2
